# Fritzing sketch arduino_bluetooth_connections (saved by Fritzing 0.9.1b)

parts:
  Part1 = Bluetooth HC-05 Macho
  Part2 = Arduino Uno (Rev3)

nets:
  N1: Part1.TXD, Part2.D0/RX
  N2: Part1.RXD, Part2.D1/TX
  VCC: Part1.VCC, Part2.5V
  GND: Part1.GND, Part2.GND

notes:
  I actually used an HC-06. The difference is that an HC-05 can act as master or slave where as an HC-05 can only act as a slave.
  Note the terminal marked TXD on the HC-06 connects to the terminal marked RXD on the Arduino (and vice versa).
